# Fritzing sketch Untitled Sketch (saved by Fritzing 0.9.3b)
breadboards: 1

parts:
  Part1 = Arduino Uno (Rev3)
  RHT1 = Humidity and Temperature Sensor RHT03
  LCD1 = LCD screen
  R1 = Rotary Potentiometer (Small) [maximum_resistance=100kΩ package=THT]
  LED1 = LED - 5mm [color="Red (633nm)" package="5 mm [THT]"]
  LED2 = LED - 5mm [color="Red (633nm)" package="5 mm [THT]"]
  LED3 = LED - 5mm [color="Red (633nm)" package="5 mm [THT]"]
  module1 = MQ-2 Gas Sensor

nets:
  N1: Part1.D8, LED1.anode
  N2: Part1.D11_PWM/MOSI, LCD1.RS
  N3: Part1.D12/MISO, LCD1.E
  N4: Part1.D13/SCK, RHT1.Data-signal
  N5: Part1.D2, LCD1.DB4
  N6: Part1.D3_PWM, LCD1.DB5
  N7: Part1.D4, LCD1.DB6
  N8: Part1.D5_PWM, LCD1.DB7
  N9: Part1.D6_PWM, LED2.anode
  N10: Part1.D7, LED3.anode
  5V: Part1.5V, RHT1.Vcc, LCD1.VDD, LCD1.LED+, R1.leg2, module1.connector7
  GND: Part1.GND, RHT1.GND_1, LCD1.VSS, LCD1.R/W, LCD1.LED-, R1.leg1, LED1.cathode, LED2.cathode, LED3.cathode, module1.connector8
  N11: LCD1.V0, R1.wiper
